# Fritzing sketch rangkaian 1 (saved by Fritzing 0.8.7b)

parts:
  S3 = Magnetic Door Switch [package=reed_switch_plastic]
  U1 = ESP8266 NodeMCU LoLin base
  M1 = fc-51 [package=THT]
  M2 = fc-51 [package=THT]

nets:
  N1: S3.1, U1.GND1-0, U1.GND2-0, U1.GND3-2, U1.GND8-5, M2.pin2
  N2: S3.2, U1.D2-0, U1.D2-3
  N3: U1.D0-0, U1.D0-2, M1.pin1
  N4: U1.D1-0, U1.D1-2, M2.pin1

custom parts:
  ESP8266 NodeMCU LoLin base: ESP8266 based NodeMCU Base
