# Fritzing sketch rangkaian 2 (saved by Fritzing 0.8.7b)

parts:
  S3 = Magnetic Door Switch [package=reed_switch_plastic]
  U1 = ESP8266 NodeMCU LoLin base
  Part1 = SRF05 Ultrasonic Rangefinder
  Part2 = SRF05 Ultrasonic Rangefinder

nets:
  N1: S3.1, U1.GND1-0, U1.GND2-0, U1.GND3-2, U1.GND8-5, Part2.GND
  N2: S3.2, U1.D5-0, U1.D5-3
  N3: U1.D1-0, U1.D1-3, Part1.Trig
  N4: U1.D2-0, U1.D2-3, Part1.Echo
  N5: U1.D3-0, U1.D3-3, Part2.Trig
  N6: U1.D4-0, Part2.Echo

custom parts:
  ESP8266 NodeMCU LoLin base: ESP8266 based NodeMCU Base
